// Logisim project TP1.circ as structural Verilog: 5 circuits, main circuit main
module main (
  input  in_1,
  input  in_2
);

  wire decodeur_1_imm_reg;
  wire [1:0] decodeur_1_op;
  wire [3:0] decodeur_1_rd, decodeur_1_rot, decodeur_1_rs1, decodeur_1_rs2;
  wire [7:0] decodeur_1_imm;
  wire [23:0] r15_pc_q_2;
  wire [31:0] add4_1_sortie, alu_1_sortie, banc_reg_1_valreg0, banc_reg_1_valreg1,
       calculateur_imm_1_imm_final, multiplexer_1_out, r15_pc_q, ram_1_dout;

  RAM #(.addrWidth(24), .asyncread("true"), .dataWidth(32)) ram_1 (
    .addr(r15_pc_q_2), .oe(1'b1), .dout(ram_1_dout));  // open: we, clk, din
  decodeur decodeur_1 (
    .Instr(ram_1_dout), .Rs1(decodeur_1_rs1), .Rs2(decodeur_1_rs2), .Rd(decodeur_1_rd), .Imm(decodeur_1_imm),
    .Rot(decodeur_1_rot), .Imm_reg(decodeur_1_imm_reg), .Op(decodeur_1_op));
  Register #(.width(32)) r15_pc (
    .D(add4_1_sortie), .clk(in_1), .Q({r15_pc_q[31:26], r15_pc_q_2, r15_pc_q[1:0]}));  // open: en, clr
  add4 add4_1 (.entree({r15_pc_q[31:26], r15_pc_q_2, r15_pc_q[1:0]}), .sortie(add4_1_sortie));
  // Probe on banc_reg_1_valreg0
  banc_reg banc_reg_1 (
    .clk(in_1), .ValEcriture(alu_1_sortie), .IndReg0(decodeur_1_rs1), .IndReg1(decodeur_1_rs2),
    .IndRegEcr(decodeur_1_rd), .SigEcr(in_2), .R15_in({r15_pc_q[31:26], r15_pc_q_2, r15_pc_q[1:0]}),
    .ValReg0(banc_reg_1_valreg0), .Valreg1(banc_reg_1_valreg1));
  // Probe on banc_reg_1_valreg1
  calculateur_imm calculateur_imm_1 (
    .imm(decodeur_1_imm), .rotate(decodeur_1_rot), .imm_final(calculateur_imm_1_imm_final));
  Multiplexer #(.width(32)) multiplexer_1 (
    .in0(banc_reg_1_valreg1), .in1(calculateur_imm_1_imm_final), .out(multiplexer_1_out),
    .sel(decodeur_1_imm_reg));
  ALU alu_1 (
    .Op1(banc_reg_1_valreg0), .Op2(multiplexer_1_out), .Sel(decodeur_1_op), .Sortie(alu_1_sortie));  // open: NZCV
endmodule

module decodeur (
  input  [31:0] Instr,
  output [3:0] Rs1,
  output [3:0] Rs2,
  output [3:0] Rd,
  output [7:0] Imm,
  output [3:0] Rot,
  output Imm_reg,
  output [1:0] Op
);

  decodeur_opcode decodeur_opcode_1 (.OpCode(Instr[24:21]), .Op(Op));

  assign Imm = Instr[7:0];
  assign Imm_reg = Instr[25];
  assign Rd = Instr[15:12];
  assign Rot = Instr[11:8];
  assign Rs1 = Instr[19:16];
  assign Rs2 = Instr[3:0];
endmodule

module decodeur_opcode (
  input  [3:0] OpCode,
  output [1:0] Op
);

  wire and_1_out, not_1_out;

  not not_1 (not_1_out, OpCode[3]);
  and and_1 (and_1_out, OpCode[2], not_1_out);
  or or_1 (Op[0], OpCode[0], OpCode[1]);
  or or_2 (Op[1], OpCode[1], and_1_out);
endmodule

module calculateur_imm (
  input  [7:0] imm,
  input  [3:0] rotate,
  output [31:0] imm_final
);

  Shifter #(.shift("rr"), .width(32)) shifter_1 (.in({{24{1'b0}}, imm}), .\dist ({rotate, 1'b0}), .out(imm_final));
endmodule

module add4 (
  input  [31:0] entree,
  output [31:0] sortie
);

  Adder #(.width(32)) adder_1 (.a(entree), .b(32'h4), .out(sortie));  // open: cin, cout
endmodule
